# Fritzing sketch colorimeter (saved by Fritzing 0.9.3b)
breadboards: 1

parts:
  Part1 = Arduino Uno (Rev3)
  S1 = Pushbutton [package="[THT]"]
  S2 = Pushbutton [package="[THT]"]
  R1 = Photocell (LDR) [package=THT]
  LED1 = LED - 5mm [color="Yellow (585nm)" package="5 mm [THT]"]
  LED2 = LED - 5mm [color="Green (565nm)" package="5 mm [THT]"]
  LED3 = LED - 5mm [color="Blue (470nm)" package="5 mm [THT]"]
  LED4 = LED - 5mm [color="Red (633nm)" package="5 mm [THT]"]
  R2 = Resistor [tolerance=±5% resistance=15k package=THT]

nets:
  N1: Part1.A4/SDA, Part1.3V3, S1.Pin_1, S1.Pin_2, S1.Pin_3, S1.Pin_4
  N2: Part1.A5/SCL, R1.pin_1, R2.Pin_0
  N3: Part1.D0/RX, Part1.GND, S2.Pin_1, S2.Pin_2, S2.Pin_3, S2.Pin_4, LED4.cathode
  N4: Part1.D2, LED1.anode
  N5: Part1.D3_PWM, LED2.anode
  N6: Part1.D4, LED3.anode
  N7: Part1.D5_PWM, LED4.anode
  N8: Part1.5V, R1.pin_0

notes:
  mrfrozenpeak
  In schmatic ,
  i have shown only one resistor.
  You can use all three(1k, 15k, 100k)
